# Fritzing sketch Schaltplan (saved by Fritzing 0.7.10b)
breadboards: 1

parts:
  Arduino1 = Arduino
  LCD1 = LCD screen
  R2 = Rotary Potentiometer (Small) [maximum_resistance=100kΩ]  # not connected
  T1 = LM35 Temperature Sensor [package="TO92 [THT]"]

nets:
  GND: Arduino1.GND, LCD1.VSS, LCD1.LED-, T1.GND
  N1: Arduino1.D13, LCD1.RS
  N2: Arduino1.D12, LCD1.R/W
  N3: Arduino1.D11, LCD1.E
  N4: Arduino1.D10, LCD1.DB0
  N5: Arduino1.D9, LCD1.DB1
  N6: Arduino1.D8, LCD1.DB2
  N7: Arduino1.D7, LCD1.DB3
  N8: Arduino1.D6, LCD1.DB4
  N9: Arduino1.D5, LCD1.DB5
  N10: Arduino1.D4, LCD1.DB6
  N11: Arduino1.D3, LCD1.DB7
  N12: Arduino1.3V3, LCD1.V0
  +5V: Arduino1.+5V, LCD1.VDD, LCD1.LED+, T1.+Vs
  N13: Arduino1.A0, T1.Vout
